// Digital circuit ALU.dig as structural Verilog
module ALU (
  input  Input1_0,
  input  Input1_1,
  input  Input1_2,
  input  Input1_3,
  input  Input1_4,
  input  Input1_5,
  input  Input1_6,
  input  Input1_7,
  input  Input1_8,
  input  Input1_9,
  input  Input1_10,
  input  Input1_11,
  input  Input1_12,
  input  Input1_13,
  input  Input1_14,
  input  Input1_15,
  input  Input2_0,
  input  Input2_1,
  input  Input2_2,
  input  Input2_3,
  input  Input2_4,
  input  Input2_5,
  input  Input2_6,
  input  Input2_7,
  input  Input2_8,
  input  Input2_9,
  input  Input2_10,
  input  Input2_11,
  input  Input2_12,
  input  Input2_13,
  input  Input2_14,
  input  Input2_15,
  input  SelectOP_0,
  input  SelectOP_1,
  input  Carry_in,
  output CarryOut,
  output Output_0,
  output Output_1,
  output Output_2,
  output Output_3,
  output Output_4,
  output Output_5,
  output Output_6,
  output Output_7,
  output Output_8,
  output Output_9,
  output Output_10,
  output Output_11,
  output Output_12,
  output Output_13,
  output Output_14,
  output Output_15
);

  wire adder_1_carry_out, substracter_1_carry_out;
  wire [15:0] adder_1_adder_0, demultiplexer_1_out_0, demultiplexer_1_out_1, demultiplexer_1_out_2,
       demultiplexer_1_out_3, demultiplexer_2_out_0, demultiplexer_2_out_1, demultiplexer_2_out_2,
       demultiplexer_2_out_3, diviser_1_div_0, multiplier_1_mul_0, substracter_1_sub_0;

  Demultiplexer #(.Selector_Bits(2), .Bits(16)) demultiplexer_1 (
    .sel({SelectOP_1, SelectOP_0}),
    .in({Input1_15, Input1_14, Input1_13, Input1_12, Input1_11, Input1_10, Input1_9, Input1_8, Input1_7, Input1_6, Input1_5, Input1_4, Input1_3, Input1_2, Input1_1, Input1_0}),
    .out_0(demultiplexer_1_out_0), .out_1(demultiplexer_1_out_1), .out_2(demultiplexer_1_out_2),
    .out_3(demultiplexer_1_out_3));
  Demultiplexer #(.Selector_Bits(2), .Bits(16)) demultiplexer_2 (
    .sel({SelectOP_1, SelectOP_0}),
    .in({Input2_15, Input2_14, Input2_13, Input2_12, Input2_11, Input2_10, Input2_9, Input2_8, Input2_7, Input2_6, Input2_5, Input2_4, Input2_3, Input2_2, Input2_1, Input2_0}),
    .out_0(demultiplexer_2_out_0), .out_1(demultiplexer_2_out_1), .out_2(demultiplexer_2_out_2),
    .out_3(demultiplexer_2_out_3));
  Adder adder_1 (
    .A_0(demultiplexer_1_out_0[0]), .A_1(demultiplexer_1_out_0[1]), .A_2(demultiplexer_1_out_0[2]),
    .A_3(demultiplexer_1_out_0[3]), .A_4(demultiplexer_1_out_0[4]), .A_5(demultiplexer_1_out_0[5]),
    .A_6(demultiplexer_1_out_0[6]), .A_7(demultiplexer_1_out_0[7]), .A_8(demultiplexer_1_out_0[8]),
    .A_9(demultiplexer_1_out_0[9]), .A_10(demultiplexer_1_out_0[10]), .A_11(demultiplexer_1_out_0[11]),
    .A_12(demultiplexer_1_out_0[12]), .A_13(demultiplexer_1_out_0[13]), .A_14(demultiplexer_1_out_0[14]),
    .A_15(demultiplexer_1_out_0[15]), .B_0(demultiplexer_2_out_0[0]), .B_1(demultiplexer_2_out_0[1]),
    .B_2(demultiplexer_2_out_0[2]), .B_3(demultiplexer_2_out_0[3]), .B_4(demultiplexer_2_out_0[4]),
    .B_5(demultiplexer_2_out_0[5]), .B_6(demultiplexer_2_out_0[6]), .B_7(demultiplexer_2_out_0[7]),
    .B_8(demultiplexer_2_out_0[8]), .B_9(demultiplexer_2_out_0[9]), .B_10(demultiplexer_2_out_0[10]),
    .B_11(demultiplexer_2_out_0[11]), .B_12(demultiplexer_2_out_0[12]), .B_13(demultiplexer_2_out_0[13]),
    .B_14(demultiplexer_2_out_0[14]), .B_15(demultiplexer_2_out_0[15]), .Carry_in(Carry_in),
    .Adder_0(adder_1_adder_0[0]), .Adder_1(adder_1_adder_0[1]), .Adder_2(adder_1_adder_0[2]),
    .Adder_3(adder_1_adder_0[3]), .Adder_4(adder_1_adder_0[4]), .Adder_5(adder_1_adder_0[5]),
    .Adder_6(adder_1_adder_0[6]), .Adder_7(adder_1_adder_0[7]), .Adder_8(adder_1_adder_0[8]),
    .Adder_9(adder_1_adder_0[9]), .Adder_10(adder_1_adder_0[10]), .Adder_11(adder_1_adder_0[11]),
    .Adder_12(adder_1_adder_0[12]), .Adder_13(adder_1_adder_0[13]), .Adder_14(adder_1_adder_0[14]),
    .Adder_15(adder_1_adder_0[15]), .Carry_out(adder_1_carry_out));
  Substracter substracter_1 (
    .A_0(demultiplexer_1_out_1[0]), .A_1(demultiplexer_1_out_1[1]), .A_2(demultiplexer_1_out_1[2]),
    .A_3(demultiplexer_1_out_1[3]), .A_4(demultiplexer_1_out_1[4]), .A_5(demultiplexer_1_out_1[5]),
    .A_6(demultiplexer_1_out_1[6]), .A_7(demultiplexer_1_out_1[7]), .A_8(demultiplexer_1_out_1[8]),
    .A_9(demultiplexer_1_out_1[9]), .A_10(demultiplexer_1_out_1[10]), .A_11(demultiplexer_1_out_1[11]),
    .A_12(demultiplexer_1_out_1[12]), .A_13(demultiplexer_1_out_1[13]), .A_14(demultiplexer_1_out_1[14]),
    .A_15(demultiplexer_1_out_1[15]), .B_0(demultiplexer_2_out_1[0]), .B_1(demultiplexer_2_out_1[1]),
    .B_2(demultiplexer_2_out_1[2]), .B_3(demultiplexer_2_out_1[3]), .B_4(demultiplexer_2_out_1[4]),
    .B_5(demultiplexer_2_out_1[5]), .B_6(demultiplexer_2_out_1[6]), .B_7(demultiplexer_2_out_1[7]),
    .B_8(demultiplexer_2_out_1[8]), .B_9(demultiplexer_2_out_1[9]), .B_10(demultiplexer_2_out_1[10]),
    .B_11(demultiplexer_2_out_1[11]), .B_12(demultiplexer_2_out_1[12]), .B_13(demultiplexer_2_out_1[13]),
    .B_14(demultiplexer_2_out_1[14]), .B_15(demultiplexer_2_out_1[15]), .Carry_in(Carry_in),
    .Carry_out(substracter_1_carry_out), .Sub_0(substracter_1_sub_0[0]), .Sub_1(substracter_1_sub_0[1]),
    .Sub_2(substracter_1_sub_0[2]), .Sub_3(substracter_1_sub_0[3]), .Sub_4(substracter_1_sub_0[4]),
    .Sub_5(substracter_1_sub_0[5]), .Sub_6(substracter_1_sub_0[6]), .Sub_7(substracter_1_sub_0[7]),
    .Sub_8(substracter_1_sub_0[8]), .Sub_9(substracter_1_sub_0[9]), .Sub_10(substracter_1_sub_0[10]),
    .Sub_11(substracter_1_sub_0[11]), .Sub_12(substracter_1_sub_0[12]), .Sub_13(substracter_1_sub_0[13]),
    .Sub_14(substracter_1_sub_0[14]), .Sub_15(substracter_1_sub_0[15]));  // open: Zero
  Multiplier multiplier_1 (
    .A_0(demultiplexer_1_out_2[0]), .A_1(demultiplexer_1_out_2[1]), .A_2(demultiplexer_1_out_2[2]),
    .A_3(demultiplexer_1_out_2[3]), .A_4(demultiplexer_1_out_2[4]), .A_5(demultiplexer_1_out_2[5]),
    .A_6(demultiplexer_1_out_2[6]), .A_7(demultiplexer_1_out_2[7]), .A_8(demultiplexer_1_out_2[8]),
    .A_9(demultiplexer_1_out_2[9]), .A_10(demultiplexer_1_out_2[10]), .A_11(demultiplexer_1_out_2[11]),
    .A_12(demultiplexer_1_out_2[12]), .A_13(demultiplexer_1_out_2[13]), .A_14(demultiplexer_1_out_2[14]),
    .A_15(demultiplexer_1_out_2[15]), .B_0(demultiplexer_2_out_2[0]), .B_1(demultiplexer_2_out_2[1]),
    .B_2(demultiplexer_2_out_2[2]), .B_3(demultiplexer_2_out_2[3]), .B_4(demultiplexer_2_out_2[4]),
    .B_5(demultiplexer_2_out_2[5]), .B_6(demultiplexer_2_out_2[6]), .B_7(demultiplexer_2_out_2[7]),
    .B_8(demultiplexer_2_out_2[8]), .B_9(demultiplexer_2_out_2[9]), .B_10(demultiplexer_2_out_2[10]),
    .B_11(demultiplexer_2_out_2[11]), .B_12(demultiplexer_2_out_2[12]), .B_13(demultiplexer_2_out_2[13]),
    .B_14(demultiplexer_2_out_2[14]), .B_15(demultiplexer_2_out_2[15]), .Mul_0(multiplier_1_mul_0[0]),
    .Mul_1(multiplier_1_mul_0[1]), .Mul_2(multiplier_1_mul_0[2]), .Mul_3(multiplier_1_mul_0[3]),
    .Mul_4(multiplier_1_mul_0[4]), .Mul_5(multiplier_1_mul_0[5]), .Mul_6(multiplier_1_mul_0[6]),
    .Mul_7(multiplier_1_mul_0[7]), .Mul_8(multiplier_1_mul_0[8]), .Mul_9(multiplier_1_mul_0[9]),
    .Mul_10(multiplier_1_mul_0[10]), .Mul_11(multiplier_1_mul_0[11]), .Mul_12(multiplier_1_mul_0[12]),
    .Mul_13(multiplier_1_mul_0[13]), .Mul_14(multiplier_1_mul_0[14]), .Mul_15(multiplier_1_mul_0[15]));
  Diviser diviser_1 (
    .A_0(demultiplexer_1_out_3[0]), .A_1(demultiplexer_1_out_3[1]), .A_2(demultiplexer_1_out_3[2]),
    .A_3(demultiplexer_1_out_3[3]), .A_4(demultiplexer_1_out_3[4]), .A_5(demultiplexer_1_out_3[5]),
    .A_6(demultiplexer_1_out_3[6]), .A_7(demultiplexer_1_out_3[7]), .A_8(demultiplexer_1_out_3[8]),
    .A_9(demultiplexer_1_out_3[9]), .A_10(demultiplexer_1_out_3[10]), .A_11(demultiplexer_1_out_3[11]),
    .A_12(demultiplexer_1_out_3[12]), .A_13(demultiplexer_1_out_3[13]), .A_14(demultiplexer_1_out_3[14]),
    .A_15(demultiplexer_1_out_3[15]), .B_0(demultiplexer_2_out_3[0]), .B_1(demultiplexer_2_out_3[1]),
    .B_2(demultiplexer_2_out_3[2]), .B_3(demultiplexer_2_out_3[3]), .B_4(demultiplexer_2_out_3[4]),
    .B_5(demultiplexer_2_out_3[5]), .B_6(demultiplexer_2_out_3[6]), .B_7(demultiplexer_2_out_3[7]),
    .B_8(demultiplexer_2_out_3[8]), .B_9(demultiplexer_2_out_3[9]), .B_10(demultiplexer_2_out_3[10]),
    .B_11(demultiplexer_2_out_3[11]), .B_12(demultiplexer_2_out_3[12]), .B_13(demultiplexer_2_out_3[13]),
    .B_14(demultiplexer_2_out_3[14]), .B_15(demultiplexer_2_out_3[15]), .Div_0(diviser_1_div_0[0]),
    .Div_1(diviser_1_div_0[1]), .Div_2(diviser_1_div_0[2]), .Div_3(diviser_1_div_0[3]),
    .Div_4(diviser_1_div_0[4]), .Div_5(diviser_1_div_0[5]), .Div_6(diviser_1_div_0[6]),
    .Div_7(diviser_1_div_0[7]), .Div_8(diviser_1_div_0[8]), .Div_9(diviser_1_div_0[9]),
    .Div_10(diviser_1_div_0[10]), .Div_11(diviser_1_div_0[11]), .Div_12(diviser_1_div_0[12]),
    .Div_13(diviser_1_div_0[13]), .Div_14(diviser_1_div_0[14]), .Div_15(diviser_1_div_0[15]));
  Multiplexer #(.Selector_Bits(2), .Bits(16)) multiplexer_1 (
    .sel({SelectOP_1, SelectOP_0}), .in_0(adder_1_adder_0), .in_1(substracter_1_sub_0),
    .in_2(multiplier_1_mul_0), .in_3(diviser_1_div_0),
    .out({Output_15, Output_14, Output_13, Output_12, Output_11, Output_10, Output_9, Output_8, Output_7, Output_6, Output_5, Output_4, Output_3, Output_2, Output_1, Output_0}));
  Multiplexer #(.Selector_Bits(2)) multiplexer_2 (
    .sel({SelectOP_1, SelectOP_0}), .in_0(adder_1_carry_out), .in_1(substracter_1_carry_out), .in_2(1'b0),
    .in_3(1'b0), .out(CarryOut));
endmodule
