// Digital circuit Computing_Sistem.dig as structural Verilog
module Computing_Sistem (
  input  Emergency_3,
  input  Flags3_0,
  input  Flags3_1,
  input  Flags3_2,
  input  Emergency_2,
  input  Flags2_0,
  input  Flags2_1,
  input  Flags2_2,
  input  Emergency_1,
  input  Flags1_0,
  input  Flags1_1,
  input  Flags1_2,
  input  Emergency_0,
  input  Flags0_0,
  input  Flags0_1,
  input  Flags0_2,
  input  SenzorMasina1_0,
  input  SenzorMasina1_1,
  input  SenzorMasina1_2,
  input  SenzorMasina2_0,
  input  SenzorMasina2_1,
  input  SenzorMasina2_2,
  input  SenzorMasina3_0,
  input  SenzorMasina3_1,
  input  SenzorMasina3_2,
  input  SenzorMasina0_0,
  input  SenzorMasina0_1,
  input  SenzorMasina0_2
);

  wire _8registers_encoded_1_output_0, _8registers_encoded_1_output_1, _8registers_encoded_1_output_2,
       _8registers_encoded_1_output_3, _8registers_encoded_1_output_4, _8registers_encoded_1_output_5,
       _8registers_encoded_1_output_6, _8registers_encoded_1_output_7, _8registers_encoded_1_output_8,
       _8registers_encoded_1_output_9, _8registers_encoded_1_output_10, _8registers_encoded_1_output_11,
       _8registers_encoded_1_output_12, _8registers_encoded_1_output_13, _8registers_encoded_1_output_14,
       _8registers_encoded_1_output_15, _16bit_mux_2to1_1_output_0, _16bit_mux_2to1_1_output_1,
       _16bit_mux_2to1_1_output_2, _16bit_mux_2to1_1_output_3, _16bit_mux_2to1_1_output_4,
       _16bit_mux_2to1_1_output_5, _16bit_mux_2to1_1_output_6, _16bit_mux_2to1_1_output_7,
       _16bit_mux_2to1_1_output_8, _16bit_mux_2to1_1_output_9, _16bit_mux_2to1_1_output_10,
       _16bit_mux_2to1_1_output_11, _16bit_mux_2to1_1_output_12, _16bit_mux_2to1_1_output_13,
       _16bit_mux_2to1_1_output_14, _16bit_mux_2to1_1_output_15, _16bit_mux_2to1_2_output_0,
       _16bit_mux_2to1_2_output_1, _16bit_mux_2to1_2_output_2, _16bit_mux_2to1_2_output_3,
       _16bit_mux_2to1_2_output_4, _16bit_mux_2to1_2_output_5, _16bit_mux_2to1_2_output_6,
       _16bit_mux_2to1_2_output_7, _16bit_mux_2to1_2_output_8, _16bit_mux_2to1_2_output_9,
       _16bit_mux_2to1_2_output_10, _16bit_mux_2to1_2_output_11, _16bit_mux_2to1_2_output_12,
       _16bit_mux_2to1_2_output_13, _16bit_mux_2to1_2_output_14, _16bit_mux_2to1_2_output_15,
       _16bit_mux_2to1_3_output_0, _16bit_mux_2to1_3_output_1, _16bit_mux_2to1_3_output_2,
       _16bit_mux_2to1_3_output_3, _16bit_mux_2to1_3_output_4, _16bit_mux_2to1_3_output_5,
       _16bit_mux_2to1_3_output_6, _16bit_mux_2to1_3_output_7, _16bit_mux_2to1_3_output_8,
       _16bit_mux_2to1_3_output_9, _16bit_mux_2to1_3_output_10, _16bit_mux_2to1_3_output_11,
       _16bit_mux_2to1_3_output_12, _16bit_mux_2to1_3_output_13, _16bit_mux_2to1_3_output_14,
       _16bit_mux_2to1_3_output_15, _16bit_register_1_q_0, _16bit_register_1_q_1, _16bit_register_1_q_2,
       _16bit_register_1_q_3, _16bit_register_1_q_4, _16bit_register_1_q_5, _16bit_register_1_q_6,
       _16bit_register_1_q_7, _16bit_register_1_q_8, _16bit_register_1_q_9, _16bit_register_1_q_10,
       _16bit_register_1_q_11, _16bit_register_1_q_12, _16bit_register_1_q_13, _16bit_register_1_q_14,
       _16bit_register_1_q_15, add_1_c_o, add_3_c_o, add_3_s, add_4_c_o, add_4_s, add_6_c_o, add_8_c_o,
       add_11_c_o, adder_1_adder_0, adder_1_adder_1, adder_1_adder_2, adder_1_adder_3, adder_1_adder_4,
       adder_1_adder_5, adder_1_adder_6, adder_1_adder_7, adder_1_adder_8, adder_1_adder_9, adder_1_adder_10,
       adder_1_adder_11, adder_1_adder_12, adder_1_adder_13, adder_1_adder_14, adder_1_adder_15,
       ALU_carryout, ALU_output_0, ALU_output_1, ALU_output_2, ALU_output_3, ALU_output_4, ALU_output_5,
       ALU_output_6, ALU_output_7, ALU_output_8, ALU_output_9, ALU_output_10, ALU_output_11, ALU_output_12,
       ALU_output_13, ALU_output_14, ALU_output_15, and_1_out, and_2_out, and_3_out, and_4_out, and_5_out,
       and_6_out, and_7_out, and_8_out, and_9_out, and_10_out, and_11_out, and_12_out, and_13_out,
       and_14_out, and_15_out, and_16_out, and_17_out, and_18_out, and_19_out, and_20_out, Cold_q,
       decoder_1_out_0, decoder_1_out_1, decoder_1_out_2, decoder_1_out_3, decoder_2_out_0, decoder_2_out_1,
       decoder_2_out_2, decoder_2_out_3, decoder_3_out_0, decoder_3_out_1, decoder_3_out_2, decoder_3_out_3,
       decoder_4_out_0, decoder_4_out_1, decoder_4_out_2, decoder_4_out_3, decoder_5_out_0, decoder_5_out_1,
       decoder_5_out_2, decoder_5_out_3, demultiplexer_1_out_0, demultiplexer_1_out_1, demultiplexer_2_out_0,
       demultiplexer_2_out_1, demultiplexer_3_out_0, demultiplexer_3_out_1, demultiplexer_4_out_0,
       demultiplexer_4_out_1, demultiplexer_5_out_0, demultiplexer_5_out_1, demultiplexer_6_out_0,
       demultiplexer_6_out_1, demultiplexer_7_out_0, demultiplexer_7_out_1, demultiplexer_8_out_0,
       demultiplexer_8_out_1, demultiplexer_9_out_0, demultiplexer_9_out_1, demultiplexer_10_out_0,
       demultiplexer_10_out_1, demultiplexer_11_out_0, demultiplexer_11_out_1, demultiplexer_12_out_0,
       demultiplexer_12_out_1, demultiplexer_13_out_0, demultiplexer_13_out_1, demultiplexer_14_out_0,
       demultiplexer_14_out_1, demultiplexer_15_out_0, demultiplexer_15_out_1, demultiplexer_16_out_0,
       demultiplexer_16_out_1, enable_counter_0_q, enable_counter_1_q, enable_counter_2_q,
       enable_counter_3_q, instructiondecoder_1_branchingcond, instructiondecoder_1_c_0,
       instructiondecoder_1_c_1, instructiondecoder_1_c_2, instructiondecoder_1_c_3,
       instructiondecoder_1_c_5, instructiondecoder_1_c_6, instructiondecoder_1_c_7,
       instructiondecoder_1_c_8, instructiondecoder_1_c_9, instructiondecoder_1_c_10,
       instructiondecoder_1_c_11, instructiondecoder_1_c_18, instructiondecoder_1_c_19,
       instructiondecoder_1_c_21, instructiondecoder_1_nextaddr_0, instructiondecoder_1_nextaddr_1,
       instructiondecoder_1_nextaddr_2, instructiondecoder_1_nextaddr_3, instructiondecoder_1_nextaddr_4,
       instructiondecoder_1_nextaddr_5, IR_q_0, IR_q_1, IR_q_2, IR_q_3, IR_q_4, IR_q_5, IR_q_6, IR_q_7,
       IR_q_8, IR_q_9, IR_q_10, IR_q_11, IR_q_12, IR_q_13, IR_q_14, IR_q_15, IR_q_16, IR_q_17, IR_q_18,
       IR_q_19, IR_q_20, IR_q_21, Memory_outdata_0, Memory_outdata_1, Memory_outdata_2, Memory_outdata_3,
       Memory_outdata_4, Memory_outdata_5, Memory_outdata_6, Memory_outdata_7, Memory_outdata_8,
       Memory_outdata_9, Memory_outdata_10, Memory_outdata_11, Memory_outdata_12, Memory_outdata_13,
       Memory_outdata_14, Memory_outdata_15, multiplexer_3_out, multiplexer_4_out, multiplexer_5_out,
       multiplexer_6_out, multiplexer_7_out, multiplexer_8_out, multiplexer_9_out, multiplexer_10_out,
       multiplexer_11_out, multiplexer_12_out, multiplexer_13_out, multiplexer_14_out, multiplexer_15_out,
       multiplexer_16_out, multiplexer_17_out, multiplexer_18_out, nand_1_out, or_1_out, or_2_out, or_3_out,
       or_4_out, or_5_out, or_6_out, or_7_out, or_8_out, or_9_out, or_10_out, PC_pc_0, PC_pc_1, PC_pc_2,
       PC_pc_3, PC_pc_4, PC_pc_5, PC_pc_6, PC_pc_7, PC_pc_8, PC_pc_9, PC_pc_10, PC_pc_11, PC_pc_12, PC_pc_13,
       PC_pc_14, PC_pc_15, Semafor_0_emergency, Semafor_1_emergency, Semafor_2_emergency,
       Semafor_3_emergency, WB_output_0, WB_output_1, WB_output_2, WB_output_3, WB_output_4, WB_output_5,
       WB_output_6, WB_output_7, WB_output_8, WB_output_9, WB_output_10, WB_output_11, WB_output_12,
       WB_output_13, WB_output_14, WB_output_15;
  wire [1:0] add_10_s, index_controller_1_index_0, index_incrementer_1_increment_0;
  wire [7:0] add_1_s, add_6_s, add_8_s, add_11_s, Semafor_0_q_0_0, Semafor_0_q_1_0, Semafor_0_q_2_0,
       Semafor_1_q_0_0, Semafor_1_q_1_0, Semafor_1_q_2_0, Semafor_2_q_0_0, Semafor_2_q_1_0, Semafor_2_q_2_0,
       Semafor_3_q_0_0, Semafor_3_q_1_0, Semafor_3_q_2_0;
  wire [15:0] add_2_s, add_5_s, add_7_s, add_9_s, add_12_s, multiplexer_1_out, multiplexer_2_out;

  _16bit_mux_2to1 _16bit_mux_2to1_1 (
    .I0_0(adder_1_adder_0), .I0_1(adder_1_adder_1), .I0_2(adder_1_adder_2), .I0_3(adder_1_adder_3),
    .I0_4(adder_1_adder_4), .I0_5(adder_1_adder_5), .I0_6(adder_1_adder_6), .I0_7(adder_1_adder_7),
    .I0_8(adder_1_adder_8), .I0_9(adder_1_adder_9), .I0_10(adder_1_adder_10), .I0_11(adder_1_adder_11),
    .I0_12(adder_1_adder_12), .I0_13(adder_1_adder_13), .I0_14(adder_1_adder_14), .I0_15(adder_1_adder_15),
    .I1_0(instructiondecoder_1_nextaddr_0), .I1_1(instructiondecoder_1_nextaddr_1),
    .I1_2(instructiondecoder_1_nextaddr_2), .I1_3(instructiondecoder_1_nextaddr_3),
    .I1_4(instructiondecoder_1_nextaddr_4), .I1_5(instructiondecoder_1_nextaddr_5), .I1_6(1'b0), .I1_7(1'b0),
    .I1_8(1'b0), .I1_9(1'b0), .I1_10(1'b0), .I1_11(1'b0), .I1_12(1'b0), .I1_13(1'b0), .I1_14(1'b0),
    .I1_15(1'b0), .Select(instructiondecoder_1_branchingcond), .Output_0(_16bit_mux_2to1_1_output_0),
    .Output_1(_16bit_mux_2to1_1_output_1), .Output_2(_16bit_mux_2to1_1_output_2),
    .Output_3(_16bit_mux_2to1_1_output_3), .Output_4(_16bit_mux_2to1_1_output_4),
    .Output_5(_16bit_mux_2to1_1_output_5), .Output_6(_16bit_mux_2to1_1_output_6),
    .Output_7(_16bit_mux_2to1_1_output_7), .Output_8(_16bit_mux_2to1_1_output_8),
    .Output_9(_16bit_mux_2to1_1_output_9), .Output_10(_16bit_mux_2to1_1_output_10),
    .Output_11(_16bit_mux_2to1_1_output_11), .Output_12(_16bit_mux_2to1_1_output_12),
    .Output_13(_16bit_mux_2to1_1_output_13), .Output_14(_16bit_mux_2to1_1_output_14),
    .Output_15(_16bit_mux_2to1_1_output_15));
  Program_Counter PC (
    .JumpAddr_0(_16bit_mux_2to1_1_output_0), .Reset(instructiondecoder_1_c_0),
    .JumpAddr_1(_16bit_mux_2to1_1_output_1), .JumpAddr_2(_16bit_mux_2to1_1_output_2),
    .JumpAddr_3(_16bit_mux_2to1_1_output_3), .JumpAddr_4(_16bit_mux_2to1_1_output_4),
    .JumpAddr_5(_16bit_mux_2to1_1_output_5), .JumpAddr_6(_16bit_mux_2to1_1_output_6),
    .JumpAddr_7(_16bit_mux_2to1_1_output_7), .JumpAddr_8(_16bit_mux_2to1_1_output_8),
    .JumpAddr_9(_16bit_mux_2to1_1_output_9), .JumpAddr_10(_16bit_mux_2to1_1_output_10),
    .JumpAddr_11(_16bit_mux_2to1_1_output_11), .JumpAddr_12(_16bit_mux_2to1_1_output_12),
    .JumpAddr_13(_16bit_mux_2to1_1_output_13), .JumpAddr_14(_16bit_mux_2to1_1_output_14),
    .JumpAddr_15(_16bit_mux_2to1_1_output_15), .PC_0(PC_pc_0), .PC_1(PC_pc_1), .PC_2(PC_pc_2),
    .PC_3(PC_pc_3), .PC_4(PC_pc_4), .PC_5(PC_pc_5), .PC_6(PC_pc_6), .PC_7(PC_pc_7), .PC_8(PC_pc_8),
    .PC_9(PC_pc_9), .PC_10(PC_pc_10), .PC_11(PC_pc_11), .PC_12(PC_pc_12), .PC_13(PC_pc_13), .PC_14(PC_pc_14),
    .PC_15(PC_pc_15));  // open: Clock
  Adder adder_1 (
    .A_0(1'b1), .A_1(1'b0), .A_2(1'b0), .A_3(1'b0), .A_4(1'b0), .A_5(1'b0), .A_6(1'b0), .A_7(1'b0),
    .A_8(1'b0), .A_9(1'b0), .A_10(1'b0), .A_11(1'b0), .A_12(1'b0), .A_13(1'b0), .A_14(1'b0), .A_15(1'b0),
    .B_0(PC_pc_0), .B_1(PC_pc_1), .B_2(PC_pc_2), .B_3(PC_pc_3), .B_4(PC_pc_4), .B_5(PC_pc_5), .B_6(PC_pc_6),
    .B_7(PC_pc_7), .B_8(PC_pc_8), .B_9(PC_pc_9), .B_10(PC_pc_10), .B_11(PC_pc_11), .B_12(PC_pc_12),
    .B_13(PC_pc_13), .B_14(PC_pc_14), .B_15(PC_pc_15), .Adder_0(adder_1_adder_0), .Adder_1(adder_1_adder_1),
    .Adder_2(adder_1_adder_2), .Adder_3(adder_1_adder_3), .Adder_4(adder_1_adder_4),
    .Adder_5(adder_1_adder_5), .Adder_6(adder_1_adder_6), .Adder_7(adder_1_adder_7),
    .Adder_8(adder_1_adder_8), .Adder_9(adder_1_adder_9), .Adder_10(adder_1_adder_10),
    .Adder_11(adder_1_adder_11), .Adder_12(adder_1_adder_12), .Adder_13(adder_1_adder_13),
    .Adder_14(adder_1_adder_14), .Adder_15(adder_1_adder_15));  // open: Carry_in, Carry_out
  Add #(.Bits(8)) add_1 (.a(Semafor_0_q_1_0), .b(Semafor_0_q_2_0), .s(add_1_s), .c_o(add_1_c_o));  // open: c_i
  Add add_2 (.a(Semafor_0_q_0_0[0]), .b(add_1_s[0]), .c_i(add_1_c_o), .s(add_2_s[0]));  // open: c_o
  or or_1 (or_1_out, Semafor_3_emergency, Semafor_2_emergency);
  or or_2 (or_2_out, Semafor_1_emergency, Semafor_0_emergency);
  Memory IR (
    .A_0(PC_pc_0), .A_1(PC_pc_1), .A_2(PC_pc_2), .A_3(PC_pc_3), .A_4(PC_pc_4), .A_5(PC_pc_5), .A_6(PC_pc_6),
    .A_7(PC_pc_7), .A_8(PC_pc_8), .A_9(PC_pc_9), .A_10(PC_pc_10), .A_11(PC_pc_11), .A_12(PC_pc_12),
    .A_13(PC_pc_13), .A_14(PC_pc_14), .A_15(PC_pc_15), .Q_7(IR_q_7), .Q_6(IR_q_6), .Q_5(IR_q_5),
    .Q_4(IR_q_4), .Q_3(IR_q_3), .Q_0(IR_q_0), .Q_1(IR_q_1), .Q_2(IR_q_2), .Q_15(IR_q_15), .Q_14(IR_q_14),
    .Q_13(IR_q_13), .Q_12(IR_q_12), .Q_11(IR_q_11), .Q_8(IR_q_8), .Q_9(IR_q_9), .Q_10(IR_q_10),
    .Q_21(IR_q_21), .Q_20(IR_q_20), .Q_19(IR_q_19), .Q_18(IR_q_18), .Q_16(IR_q_16), .Q_17(IR_q_17));
  or or_3 (or_3_out, or_1_out, or_2_out);
  Semafor Semafor_0 (
    .Enable_counters(enable_counter_0_q), .Reset_counters(and_17_out), .Async_counter1(SenzorMasina0_2),
    .Async_counter2(SenzorMasina0_1), .Async_counter3(SenzorMasina0_0), .Flag_sensor1(Flags0_2),
    .Flag_sensor2(Flags0_1), .Flag_sensor3(Flags0_0), .Emergency_sensor(Emergency_0), .Set_verde(and_9_out),
    .Set_galben(and_5_out), .Set_rosu(and_1_out), .Begin(instructiondecoder_1_c_0),
    .Q_0_0(Semafor_0_q_0_0[0]), .Q_0_1(Semafor_0_q_0_0[1]), .Q_0_2(Semafor_0_q_0_0[2]),
    .Q_0_3(Semafor_0_q_0_0[3]), .Q_0_4(Semafor_0_q_0_0[4]), .Q_0_5(Semafor_0_q_0_0[5]),
    .Q_0_6(Semafor_0_q_0_0[6]), .Q_0_7(Semafor_0_q_0_0[7]), .Q_1_0(Semafor_0_q_1_0[0]),
    .Q_1_1(Semafor_0_q_1_0[1]), .Q_1_2(Semafor_0_q_1_0[2]), .Q_1_3(Semafor_0_q_1_0[3]),
    .Q_1_4(Semafor_0_q_1_0[4]), .Q_1_5(Semafor_0_q_1_0[5]), .Q_1_6(Semafor_0_q_1_0[6]),
    .Q_1_7(Semafor_0_q_1_0[7]), .Q_2_0(Semafor_0_q_2_0[0]), .Q_2_1(Semafor_0_q_2_0[1]),
    .Q_2_2(Semafor_0_q_2_0[2]), .Q_2_3(Semafor_0_q_2_0[3]), .Q_2_4(Semafor_0_q_2_0[4]),
    .Q_2_5(Semafor_0_q_2_0[5]), .Q_2_6(Semafor_0_q_2_0[6]), .Q_2_7(Semafor_0_q_2_0[7]),
    .Emergency(Semafor_0_emergency));  // open: Flag_1, Flag_2, Flag_3, Color_green, Color_yellow, Color_red
  Add add_3 (.a(add_7_s[0]), .b(add_2_s[0]), .s(add_3_s), .c_o(add_3_c_o));  // open: c_i
  Add add_4 (.a(add_9_s[0]), .b(add_3_s), .c_i(add_3_c_o), .s(add_4_s), .c_o(add_4_c_o));
  Add add_5 (.a(add_12_s[0]), .b(add_4_s), .c_i(add_4_c_o), .s(add_5_s[0]));  // open: c_o
  Add #(.Bits(8)) add_6 (.a(Semafor_1_q_1_0), .b(Semafor_1_q_2_0), .s(add_6_s), .c_o(add_6_c_o));  // open: c_i
  Add add_7 (.a(Semafor_1_q_0_0[0]), .b(add_6_s[0]), .c_i(add_6_c_o), .s(add_7_s[0]));  // open: c_o
  buf and_1 (and_1_out, decoder_1_out_0);  // And open: In_2
  buf and_2 (and_2_out, decoder_1_out_1);  // And open: In_2
  Decoder #(.Selector_Bits(2)) decoder_1 (
    .sel(index_controller_1_index_0), .out_0(decoder_1_out_0), .out_1(decoder_1_out_1),
    .out_2(decoder_1_out_2), .out_3(decoder_1_out_3));
  buf and_3 (and_3_out, decoder_1_out_2);  // And open: In_2
  Semafor Semafor_1 (
    .Enable_counters(enable_counter_1_q), .Reset_counters(and_18_out), .Async_counter2(SenzorMasina1_2),
    .Async_counter3(SenzorMasina1_1), .Async_counter1(SenzorMasina1_0), .Flag_sensor1(Flags1_2),
    .Flag_sensor2(Flags1_1), .Flag_sensor3(Flags1_0), .Emergency_sensor(Emergency_1), .Set_verde(and_10_out),
    .Set_galben(and_6_out), .Set_rosu(and_2_out), .Begin(instructiondecoder_1_c_0),
    .Q_0_0(Semafor_1_q_0_0[0]), .Q_0_1(Semafor_1_q_0_0[1]), .Q_0_2(Semafor_1_q_0_0[2]),
    .Q_0_3(Semafor_1_q_0_0[3]), .Q_0_4(Semafor_1_q_0_0[4]), .Q_0_5(Semafor_1_q_0_0[5]),
    .Q_0_6(Semafor_1_q_0_0[6]), .Q_0_7(Semafor_1_q_0_0[7]), .Q_1_0(Semafor_1_q_1_0[0]),
    .Q_1_1(Semafor_1_q_1_0[1]), .Q_1_2(Semafor_1_q_1_0[2]), .Q_1_3(Semafor_1_q_1_0[3]),
    .Q_1_4(Semafor_1_q_1_0[4]), .Q_1_5(Semafor_1_q_1_0[5]), .Q_1_6(Semafor_1_q_1_0[6]),
    .Q_1_7(Semafor_1_q_1_0[7]), .Q_2_0(Semafor_1_q_2_0[0]), .Q_2_1(Semafor_1_q_2_0[1]),
    .Q_2_2(Semafor_1_q_2_0[2]), .Q_2_3(Semafor_1_q_2_0[3]), .Q_2_4(Semafor_1_q_2_0[4]),
    .Q_2_5(Semafor_1_q_2_0[5]), .Q_2_6(Semafor_1_q_2_0[6]), .Q_2_7(Semafor_1_q_2_0[7]),
    .Emergency(Semafor_1_emergency));  // open: Flag_1, Flag_2, Flag_3, Color_green, Color_yellow, Color_red
  and and_4 (and_4_out, decoder_1_out_3, instructiondecoder_1_c_5);
  and and_5 (and_5_out, decoder_2_out_0, instructiondecoder_1_c_9);
  and and_6 (and_6_out, decoder_2_out_1, instructiondecoder_1_c_9);
  Decoder #(.Selector_Bits(2)) decoder_2 (
    .sel(index_controller_1_index_0), .out_0(decoder_2_out_0), .out_1(decoder_2_out_1),
    .out_2(decoder_2_out_2), .out_3(decoder_2_out_3));
  and and_7 (and_7_out, decoder_2_out_2, instructiondecoder_1_c_9);
  and and_8 (and_8_out, decoder_2_out_3, instructiondecoder_1_c_9);
  Add #(.Bits(8)) add_8 (.a(Semafor_2_q_1_0), .b(Semafor_2_q_2_0), .s(add_8_s), .c_o(add_8_c_o));  // open: c_i
  Add add_9 (.a(Semafor_2_q_0_0[0]), .b(add_8_s[0]), .c_i(add_8_c_o), .s(add_9_s[0]));  // open: c_o
  nand nand_1 (nand_1_out, index_controller_1_index_0[0], index_controller_1_index_0[1]);
  InstructionDecoder instructiondecoder_1 (
    .CS_0(IR_q_0), .CS_1(IR_q_1), .CS_2(IR_q_2), .CS_3(IR_q_3), .Emergency(or_3_out),
    .emergency_0(Semafor_0_emergency), .emergency_1(Semafor_1_emergency), .emergency_2(Semafor_2_emergency),
    .emergency_3(Semafor_3_emergency), .cold(Cold_q), .T_verde_lt_T_min(ALU_carryout),
    .T_verde_gt_T_max(ALU_carryout), .index__eq_3(nand_1_out), .Emergency_4(or_3_out), .BA_0(IR_q_4),
    .BA_1(IR_q_5), .BA_2(IR_q_6), .BA_3(IR_q_7), .BA_4(IR_q_8), .BA_5(IR_q_9), .CF_0(IR_q_10),
    .CF_1(IR_q_11), .CF_2(IR_q_12), .CF_3(IR_q_13), .CF_4(IR_q_14), .CF_5(IR_q_15), .CF_6(IR_q_16),
    .CF_7(IR_q_17), .CF_8(IR_q_18), .CF_9(IR_q_19), .CF_10(IR_q_20), .CF_11(IR_q_21),
    .BranchingCond(instructiondecoder_1_branchingcond), .NextAddr_0(instructiondecoder_1_nextaddr_0),
    .NextAddr_1(instructiondecoder_1_nextaddr_1), .NextAddr_2(instructiondecoder_1_nextaddr_2),
    .NextAddr_3(instructiondecoder_1_nextaddr_3), .NextAddr_4(instructiondecoder_1_nextaddr_4),
    .NextAddr_5(instructiondecoder_1_nextaddr_5), .C_0(instructiondecoder_1_c_0),
    .C_1(instructiondecoder_1_c_1), .C_2(instructiondecoder_1_c_2), .C_3(instructiondecoder_1_c_3),
    .C_5(instructiondecoder_1_c_5), .C_6(instructiondecoder_1_c_6), .C_7(instructiondecoder_1_c_7),
    .C_8(instructiondecoder_1_c_8), .C_9(instructiondecoder_1_c_9), .C_10(instructiondecoder_1_c_10),
    .C_11(instructiondecoder_1_c_11), .C_18(instructiondecoder_1_c_18), .C_19(instructiondecoder_1_c_19),
    .C_21(instructiondecoder_1_c_21));  // open: T_verde, Debit, T_galben, C_4, C_12, C_13, C_14, C_15, C_16, C_17, C_20, C_22, C_23, C_24
  and and_9 (and_9_out, decoder_3_out_0, instructiondecoder_1_c_2);
  RS_FF_AS Cold (.S(instructiondecoder_1_c_0), .R(instructiondecoder_1_c_19), .Q(Cold_q));  // open: nQ
  Semafor Semafor_2 (
    .Enable_counters(enable_counter_2_q), .Reset_counters(and_19_out), .Async_counter2(SenzorMasina2_2),
    .Async_counter3(SenzorMasina2_1), .Async_counter1(SenzorMasina2_0), .Flag_sensor1(Flags2_2),
    .Flag_sensor2(Flags2_1), .Flag_sensor3(Flags2_0), .Emergency_sensor(Emergency_2), .Set_verde(and_11_out),
    .Set_galben(and_7_out), .Set_rosu(and_3_out), .Begin(instructiondecoder_1_c_0),
    .Q_0_0(Semafor_2_q_0_0[0]), .Q_0_1(Semafor_2_q_0_0[1]), .Q_0_2(Semafor_2_q_0_0[2]),
    .Q_0_3(Semafor_2_q_0_0[3]), .Q_0_4(Semafor_2_q_0_0[4]), .Q_0_5(Semafor_2_q_0_0[5]),
    .Q_0_6(Semafor_2_q_0_0[6]), .Q_0_7(Semafor_2_q_0_0[7]), .Q_1_0(Semafor_2_q_1_0[0]),
    .Q_1_1(Semafor_2_q_1_0[1]), .Q_1_2(Semafor_2_q_1_0[2]), .Q_1_3(Semafor_2_q_1_0[3]),
    .Q_1_4(Semafor_2_q_1_0[4]), .Q_1_5(Semafor_2_q_1_0[5]), .Q_1_6(Semafor_2_q_1_0[6]),
    .Q_1_7(Semafor_2_q_1_0[7]), .Q_2_0(Semafor_2_q_2_0[0]), .Q_2_1(Semafor_2_q_2_0[1]),
    .Q_2_2(Semafor_2_q_2_0[2]), .Q_2_3(Semafor_2_q_2_0[3]), .Q_2_4(Semafor_2_q_2_0[4]),
    .Q_2_5(Semafor_2_q_2_0[5]), .Q_2_6(Semafor_2_q_2_0[6]), .Q_2_7(Semafor_2_q_2_0[7]),
    .Emergency(Semafor_2_emergency));  // open: Flag_1, Flag_2, Flag_3, Color_green, Color_yellow, Color_red
  and and_10 (and_10_out, decoder_3_out_1, instructiondecoder_1_c_2);
  Decoder #(.Selector_Bits(2)) decoder_3 (
    .sel(index_controller_1_index_0), .out_0(decoder_3_out_0), .out_1(decoder_3_out_1),
    .out_2(decoder_3_out_2), .out_3(decoder_3_out_3));
  and and_11 (and_11_out, decoder_3_out_2, instructiondecoder_1_c_2);
  and and_12 (and_12_out, decoder_3_out_3, instructiondecoder_1_c_2);
  or or_4 (or_4_out, instructiondecoder_1_c_6, or_5_out);
  or or_5 (or_5_out, instructiondecoder_1_c_7, instructiondecoder_1_c_8);
  Add #(.Bits(2)) add_10 (
    .a(index_controller_1_index_0), .b(index_incrementer_1_increment_0), .s(add_10_s));  // open: c_i, c_o
  or or_6 (or_6_out, or_4_out, instructiondecoder_1_c_18);
  or or_7 (or_7_out, decoder_4_out_0, instructiondecoder_1_c_21);
  Index_controller index_controller_1 (
    .D_0(add_10_s[0]), .D_1(add_10_s[1]), .Reset(instructiondecoder_1_c_0), .Increment(or_6_out),
    .Override(or_4_out), .index_0(index_controller_1_index_0[0]), .index_1(index_controller_1_index_0[1]));
  RS_FF_AS enable_counter_0 (.S(and_13_out), .R(instructiondecoder_1_c_9), .Q(enable_counter_0_q));  // open: nQ
  and and_13 (and_13_out, or_7_out, instructiondecoder_1_c_1);
  or or_8 (or_8_out, decoder_4_out_1, instructiondecoder_1_c_21);
  Add #(.Bits(8)) add_11 (.a(Semafor_3_q_1_0), .b(Semafor_3_q_2_0), .s(add_11_s), .c_o(add_11_c_o));  // open: c_i
  Add add_12 (.a(Semafor_3_q_0_0[0]), .b(add_11_s[0]), .c_i(add_11_c_o), .s(add_12_s[0]));  // open: c_o
  index_incrementer index_incrementer_1 (
    .C_6(instructiondecoder_1_c_6), .C_7(instructiondecoder_1_c_7), .C_8(instructiondecoder_1_c_8),
    .increment_0(index_incrementer_1_increment_0[0]), .increment_1(index_incrementer_1_increment_0[1]));
  RS_FF_AS enable_counter_1 (.S(and_14_out), .R(instructiondecoder_1_c_9), .Q(enable_counter_1_q));  // open: nQ
  and and_14 (and_14_out, or_8_out, instructiondecoder_1_c_1);
  or or_9 (or_9_out, decoder_4_out_2, instructiondecoder_1_c_21);
  Decoder #(.Selector_Bits(2)) decoder_4 (
    .sel(index_controller_1_index_0), .out_0(decoder_4_out_0), .out_1(decoder_4_out_1),
    .out_2(decoder_4_out_2), .out_3(decoder_4_out_3));
  Multiplexer #(.Bits(16), .Selector_Bits(2)) multiplexer_1 (
    .in_0(add_2_s), .in_1(add_7_s), .in_2(add_9_s), .in_3(add_12_s), .out(multiplexer_1_out));  // open: sel
  RS_FF_AS enable_counter_2 (.S(and_15_out), .R(instructiondecoder_1_c_9), .Q(enable_counter_2_q));  // open: nQ
  and and_15 (and_15_out, or_9_out, instructiondecoder_1_c_1);
  or or_10 (or_10_out, decoder_4_out_3, instructiondecoder_1_c_21);
  _16bit_mux_2to1 _16bit_mux_2to1_2 (
    .I0_0(ALU_output_0), .I0_1(ALU_output_1), .I0_2(ALU_output_2), .I0_3(ALU_output_3), .I0_4(ALU_output_4),
    .I0_5(ALU_output_5), .I0_6(ALU_output_6), .I0_7(ALU_output_7), .I0_8(ALU_output_8), .I0_9(ALU_output_9),
    .I0_10(ALU_output_10), .I0_11(ALU_output_11), .I0_12(ALU_output_12), .I0_13(ALU_output_13),
    .I0_14(ALU_output_14), .I0_15(ALU_output_15), .I1_0(WB_output_0), .I1_1(WB_output_1), .I1_2(WB_output_2),
    .I1_3(WB_output_3), .I1_4(WB_output_4), .I1_5(WB_output_5), .I1_6(WB_output_6), .I1_7(WB_output_7),
    .I1_8(WB_output_8), .I1_9(WB_output_9), .I1_10(WB_output_10), .I1_11(WB_output_11), .I1_12(WB_output_12),
    .I1_13(WB_output_13), .I1_14(WB_output_14), .I1_15(WB_output_15), .Output_0(_16bit_mux_2to1_2_output_0),
    .Output_1(_16bit_mux_2to1_2_output_1), .Output_2(_16bit_mux_2to1_2_output_2),
    .Output_3(_16bit_mux_2to1_2_output_3), .Output_4(_16bit_mux_2to1_2_output_4),
    .Output_5(_16bit_mux_2to1_2_output_5), .Output_6(_16bit_mux_2to1_2_output_6),
    .Output_7(_16bit_mux_2to1_2_output_7), .Output_8(_16bit_mux_2to1_2_output_8),
    .Output_9(_16bit_mux_2to1_2_output_9), .Output_10(_16bit_mux_2to1_2_output_10),
    .Output_11(_16bit_mux_2to1_2_output_11), .Output_12(_16bit_mux_2to1_2_output_12),
    .Output_13(_16bit_mux_2to1_2_output_13), .Output_14(_16bit_mux_2to1_2_output_14),
    .Output_15(_16bit_mux_2to1_2_output_15));  // open: Select
  RS_FF_AS enable_counter_3 (.S(and_16_out), .R(instructiondecoder_1_c_9), .Q(enable_counter_3_q));  // open: nQ
  and and_16 (and_16_out, or_10_out, instructiondecoder_1_c_1);
  Semafor Semafor_3 (
    .Enable_counters(enable_counter_3_q), .Reset_counters(and_20_out), .Async_counter2(SenzorMasina3_2),
    .Async_counter3(SenzorMasina3_1), .Async_counter1(SenzorMasina3_0), .Flag_sensor1(Flags3_2),
    .Flag_sensor2(Flags3_1), .Flag_sensor3(Flags3_0), .Emergency_sensor(Emergency_3), .Set_verde(and_12_out),
    .Set_galben(and_8_out), .Set_rosu(and_4_out), .Begin(instructiondecoder_1_c_0),
    .Q_0_0(Semafor_3_q_0_0[0]), .Q_0_1(Semafor_3_q_0_0[1]), .Q_0_2(Semafor_3_q_0_0[2]),
    .Q_0_3(Semafor_3_q_0_0[3]), .Q_0_4(Semafor_3_q_0_0[4]), .Q_0_5(Semafor_3_q_0_0[5]),
    .Q_0_6(Semafor_3_q_0_0[6]), .Q_0_7(Semafor_3_q_0_0[7]), .Q_1_0(Semafor_3_q_1_0[0]),
    .Q_1_1(Semafor_3_q_1_0[1]), .Q_1_2(Semafor_3_q_1_0[2]), .Q_1_3(Semafor_3_q_1_0[3]),
    .Q_1_4(Semafor_3_q_1_0[4]), .Q_1_5(Semafor_3_q_1_0[5]), .Q_1_6(Semafor_3_q_1_0[6]),
    .Q_1_7(Semafor_3_q_1_0[7]), .Q_2_0(Semafor_3_q_2_0[0]), .Q_2_1(Semafor_3_q_2_0[1]),
    .Q_2_2(Semafor_3_q_2_0[2]), .Q_2_3(Semafor_3_q_2_0[3]), .Q_2_4(Semafor_3_q_2_0[4]),
    .Q_2_5(Semafor_3_q_2_0[5]), .Q_2_6(Semafor_3_q_2_0[6]), .Q_2_7(Semafor_3_q_2_0[7]),
    .Emergency(Semafor_3_emergency));  // open: Flag_1, Flag_2, Flag_3, Color_green, Color_yellow, Color_red
  _8Registers_encoded _8registers_encoded_1 (
    .Input_0(_16bit_mux_2to1_2_output_0), .Input_1(_16bit_mux_2to1_2_output_1),
    .Input_2(_16bit_mux_2to1_2_output_2), .Input_3(_16bit_mux_2to1_2_output_3),
    .Input_4(_16bit_mux_2to1_2_output_4), .Input_5(_16bit_mux_2to1_2_output_5),
    .Input_6(_16bit_mux_2to1_2_output_6), .Input_7(_16bit_mux_2to1_2_output_7),
    .Input_8(_16bit_mux_2to1_2_output_8), .Input_9(_16bit_mux_2to1_2_output_9),
    .Input_10(_16bit_mux_2to1_2_output_10), .Input_11(_16bit_mux_2to1_2_output_11),
    .Input_12(_16bit_mux_2to1_2_output_12), .Input_13(_16bit_mux_2to1_2_output_13),
    .Input_14(_16bit_mux_2to1_2_output_14), .Input_15(_16bit_mux_2to1_2_output_15),
    .Reset(instructiondecoder_1_c_0), .Output_0(_8registers_encoded_1_output_0),
    .Output_1(_8registers_encoded_1_output_1), .Output_2(_8registers_encoded_1_output_2),
    .Output_3(_8registers_encoded_1_output_3), .Output_4(_8registers_encoded_1_output_4),
    .Output_5(_8registers_encoded_1_output_5), .Output_6(_8registers_encoded_1_output_6),
    .Output_7(_8registers_encoded_1_output_7), .Output_8(_8registers_encoded_1_output_8),
    .Output_9(_8registers_encoded_1_output_9), .Output_10(_8registers_encoded_1_output_10),
    .Output_11(_8registers_encoded_1_output_11), .Output_12(_8registers_encoded_1_output_12),
    .Output_13(_8registers_encoded_1_output_13), .Output_14(_8registers_encoded_1_output_14),
    .Output_15(_8registers_encoded_1_output_15));  // open: Select_input_0, Select_input_1, Select_input_2, Select_output_0, Select_output_1, Select_output_2, Clock
  Multiplexer #(.Bits(16)) multiplexer_2 (
    .sel(instructiondecoder_1_c_11), .in_0(multiplexer_1_out), .in_1(add_5_s), .out(multiplexer_2_out));
  _16bit_mux_2to1 _16bit_mux_2to1_3 (
    .I0_0(_16bit_register_1_q_0), .I0_1(_16bit_register_1_q_1), .I0_2(_16bit_register_1_q_2),
    .I0_3(_16bit_register_1_q_3), .I0_4(_16bit_register_1_q_4), .I0_5(_16bit_register_1_q_5),
    .I0_6(_16bit_register_1_q_6), .I0_7(_16bit_register_1_q_7), .I0_8(_16bit_register_1_q_8),
    .I0_9(_16bit_register_1_q_9), .I0_10(_16bit_register_1_q_10), .I0_11(_16bit_register_1_q_11),
    .I0_12(_16bit_register_1_q_12), .I0_13(_16bit_register_1_q_13), .I0_14(_16bit_register_1_q_14),
    .I0_15(_16bit_register_1_q_15), .I1_0(multiplexer_2_out[0]), .I1_1(multiplexer_2_out[1]),
    .I1_2(multiplexer_2_out[2]), .I1_3(multiplexer_2_out[3]), .I1_4(multiplexer_2_out[4]),
    .I1_5(multiplexer_2_out[5]), .I1_6(multiplexer_2_out[6]), .I1_7(multiplexer_2_out[7]),
    .I1_8(multiplexer_2_out[8]), .I1_9(multiplexer_2_out[9]), .I1_10(multiplexer_2_out[10]),
    .I1_11(multiplexer_2_out[11]), .I1_12(multiplexer_2_out[12]), .I1_13(multiplexer_2_out[13]),
    .I1_14(multiplexer_2_out[14]), .I1_15(multiplexer_2_out[15]), .Select(instructiondecoder_1_c_10),
    .Output_0(_16bit_mux_2to1_3_output_0), .Output_1(_16bit_mux_2to1_3_output_1),
    .Output_2(_16bit_mux_2to1_3_output_2), .Output_3(_16bit_mux_2to1_3_output_3),
    .Output_4(_16bit_mux_2to1_3_output_4), .Output_5(_16bit_mux_2to1_3_output_5),
    .Output_6(_16bit_mux_2to1_3_output_6), .Output_7(_16bit_mux_2to1_3_output_7),
    .Output_8(_16bit_mux_2to1_3_output_8), .Output_9(_16bit_mux_2to1_3_output_9),
    .Output_10(_16bit_mux_2to1_3_output_10), .Output_11(_16bit_mux_2to1_3_output_11),
    .Output_12(_16bit_mux_2to1_3_output_12), .Output_13(_16bit_mux_2to1_3_output_13),
    .Output_14(_16bit_mux_2to1_3_output_14), .Output_15(_16bit_mux_2to1_3_output_15));
  ALU ALU (
    .Input1_0(_16bit_mux_2to1_3_output_0), .Input1_1(_16bit_mux_2to1_3_output_1),
    .Input1_2(_16bit_mux_2to1_3_output_2), .Input1_3(_16bit_mux_2to1_3_output_3),
    .Input1_4(_16bit_mux_2to1_3_output_4), .Input1_5(_16bit_mux_2to1_3_output_5),
    .Input1_6(_16bit_mux_2to1_3_output_6), .Input1_7(_16bit_mux_2to1_3_output_7),
    .Input1_8(_16bit_mux_2to1_3_output_8), .Input1_9(_16bit_mux_2to1_3_output_9),
    .Input1_10(_16bit_mux_2to1_3_output_10), .Input1_11(_16bit_mux_2to1_3_output_11),
    .Input1_12(_16bit_mux_2to1_3_output_12), .Input1_13(_16bit_mux_2to1_3_output_13),
    .Input1_14(_16bit_mux_2to1_3_output_14), .Input1_15(_16bit_mux_2to1_3_output_15),
    .Input2_0(_8registers_encoded_1_output_0), .Input2_1(_8registers_encoded_1_output_1),
    .Input2_2(_8registers_encoded_1_output_2), .Input2_3(_8registers_encoded_1_output_3),
    .Input2_4(_8registers_encoded_1_output_4), .Input2_5(_8registers_encoded_1_output_5),
    .Input2_6(_8registers_encoded_1_output_6), .Input2_7(_8registers_encoded_1_output_7),
    .Input2_8(_8registers_encoded_1_output_8), .Input2_9(_8registers_encoded_1_output_9),
    .Input2_10(_8registers_encoded_1_output_10), .Input2_11(_8registers_encoded_1_output_11),
    .Input2_12(_8registers_encoded_1_output_12), .Input2_13(_8registers_encoded_1_output_13),
    .Input2_14(_8registers_encoded_1_output_14), .Input2_15(_8registers_encoded_1_output_15),
    .CarryOut(ALU_carryout), .Output_0(ALU_output_0), .Output_1(ALU_output_1), .Output_2(ALU_output_2),
    .Output_3(ALU_output_3), .Output_4(ALU_output_4), .Output_5(ALU_output_5), .Output_6(ALU_output_6),
    .Output_7(ALU_output_7), .Output_8(ALU_output_8), .Output_9(ALU_output_9), .Output_10(ALU_output_10),
    .Output_11(ALU_output_11), .Output_12(ALU_output_12), .Output_13(ALU_output_13),
    .Output_14(ALU_output_14), .Output_15(ALU_output_15));  // open: SelectOP_0, SelectOP_1, Carry_in
  and and_17 (and_17_out, decoder_5_out_0, instructiondecoder_1_c_3);
  and and_18 (and_18_out, decoder_5_out_1, instructiondecoder_1_c_3);
  Decoder #(.Selector_Bits(2)) decoder_5 (
    .sel(index_controller_1_index_0), .out_0(decoder_5_out_0), .out_1(decoder_5_out_1),
    .out_2(decoder_5_out_2), .out_3(decoder_5_out_3));
  and and_19 (and_19_out, decoder_5_out_2, instructiondecoder_1_c_3);
  _16bit_register _16bit_register_1 (
    .D_0(ALU_output_0), .D_1(ALU_output_1), .D_2(ALU_output_2), .D_3(ALU_output_3), .D_4(ALU_output_4),
    .D_5(ALU_output_5), .D_6(ALU_output_6), .D_7(ALU_output_7), .D_8(ALU_output_8), .D_9(ALU_output_9),
    .D_10(ALU_output_10), .D_11(ALU_output_11), .D_12(ALU_output_12), .D_13(ALU_output_13),
    .D_14(ALU_output_14), .D_15(ALU_output_15), .Reset(instructiondecoder_1_c_0),
    .Q_0(_16bit_register_1_q_0), .Q_1(_16bit_register_1_q_1), .Q_2(_16bit_register_1_q_2),
    .Q_3(_16bit_register_1_q_3), .Q_4(_16bit_register_1_q_4), .Q_5(_16bit_register_1_q_5),
    .Q_6(_16bit_register_1_q_6), .Q_7(_16bit_register_1_q_7), .Q_8(_16bit_register_1_q_8),
    .Q_9(_16bit_register_1_q_9), .Q_10(_16bit_register_1_q_10), .Q_11(_16bit_register_1_q_11),
    .Q_12(_16bit_register_1_q_12), .Q_13(_16bit_register_1_q_13), .Q_14(_16bit_register_1_q_14),
    .Q_15(_16bit_register_1_q_15));  // open: Clock
  and and_20 (and_20_out, decoder_5_out_3, instructiondecoder_1_c_3);
  Demultiplexer demultiplexer_1 (
    .in(ALU_output_0), .out_0(demultiplexer_1_out_0), .out_1(demultiplexer_1_out_1));  // open: sel
  Demultiplexer demultiplexer_2 (
    .in(ALU_output_1), .out_0(demultiplexer_2_out_0), .out_1(demultiplexer_2_out_1));  // open: sel
  Demultiplexer demultiplexer_3 (
    .in(ALU_output_2), .out_0(demultiplexer_3_out_0), .out_1(demultiplexer_3_out_1));  // open: sel
  Demultiplexer demultiplexer_4 (
    .in(ALU_output_3), .out_0(demultiplexer_4_out_0), .out_1(demultiplexer_4_out_1));  // open: sel
  Demultiplexer demultiplexer_5 (
    .in(ALU_output_4), .out_0(demultiplexer_5_out_0), .out_1(demultiplexer_5_out_1));  // open: sel
  Demultiplexer demultiplexer_6 (
    .in(ALU_output_5), .out_0(demultiplexer_6_out_0), .out_1(demultiplexer_6_out_1));  // open: sel
  Demultiplexer demultiplexer_7 (
    .in(ALU_output_6), .out_0(demultiplexer_7_out_0), .out_1(demultiplexer_7_out_1));  // open: sel
  Demultiplexer demultiplexer_8 (
    .in(ALU_output_7), .out_0(demultiplexer_8_out_0), .out_1(demultiplexer_8_out_1));  // open: sel
  Demultiplexer demultiplexer_9 (
    .in(ALU_output_8), .out_0(demultiplexer_9_out_0), .out_1(demultiplexer_9_out_1));  // open: sel
  Demultiplexer demultiplexer_10 (
    .in(ALU_output_9), .out_0(demultiplexer_10_out_0), .out_1(demultiplexer_10_out_1));  // open: sel
  Demultiplexer demultiplexer_11 (
    .in(ALU_output_10), .out_0(demultiplexer_11_out_0), .out_1(demultiplexer_11_out_1));  // open: sel
  Demultiplexer demultiplexer_12 (
    .in(ALU_output_11), .out_0(demultiplexer_12_out_0), .out_1(demultiplexer_12_out_1));  // open: sel
  Demultiplexer demultiplexer_13 (
    .in(ALU_output_12), .out_0(demultiplexer_13_out_0), .out_1(demultiplexer_13_out_1));  // open: sel
  Demultiplexer demultiplexer_14 (
    .in(ALU_output_13), .out_0(demultiplexer_14_out_0), .out_1(demultiplexer_14_out_1));  // open: sel
  Demultiplexer demultiplexer_15 (
    .in(ALU_output_14), .out_0(demultiplexer_15_out_0), .out_1(demultiplexer_15_out_1));  // open: sel
  Demultiplexer demultiplexer_16 (
    .in(ALU_output_15), .out_0(demultiplexer_16_out_0), .out_1(demultiplexer_16_out_1));  // open: sel
  Multiplexer multiplexer_3 (
    .in_0(demultiplexer_1_out_1), .in_1(_8registers_encoded_1_output_0), .out(multiplexer_3_out));  // open: sel
  Multiplexer multiplexer_4 (
    .in_0(demultiplexer_2_out_1), .in_1(_8registers_encoded_1_output_1), .out(multiplexer_4_out));  // open: sel
  Multiplexer multiplexer_5 (
    .in_0(demultiplexer_3_out_1), .in_1(_8registers_encoded_1_output_2), .out(multiplexer_5_out));  // open: sel
  Multiplexer multiplexer_6 (
    .in_0(demultiplexer_4_out_1), .in_1(_8registers_encoded_1_output_3), .out(multiplexer_6_out));  // open: sel
  Multiplexer multiplexer_7 (
    .in_0(demultiplexer_5_out_1), .in_1(_8registers_encoded_1_output_4), .out(multiplexer_7_out));  // open: sel
  Multiplexer multiplexer_8 (
    .in_0(demultiplexer_6_out_1), .in_1(_8registers_encoded_1_output_5), .out(multiplexer_8_out));  // open: sel
  Multiplexer multiplexer_9 (
    .in_0(demultiplexer_7_out_1), .in_1(_8registers_encoded_1_output_6), .out(multiplexer_9_out));  // open: sel
  Multiplexer multiplexer_10 (
    .in_0(demultiplexer_8_out_1), .in_1(_8registers_encoded_1_output_7), .out(multiplexer_10_out));  // open: sel
  Multiplexer multiplexer_11 (
    .in_0(demultiplexer_9_out_1), .in_1(_8registers_encoded_1_output_8), .out(multiplexer_11_out));  // open: sel
  Multiplexer multiplexer_12 (
    .in_0(demultiplexer_10_out_1), .in_1(_8registers_encoded_1_output_9), .out(multiplexer_12_out));  // open: sel
  Multiplexer multiplexer_13 (
    .in_0(demultiplexer_11_out_1), .in_1(_8registers_encoded_1_output_10), .out(multiplexer_13_out));  // open: sel
  Multiplexer multiplexer_14 (
    .in_0(demultiplexer_12_out_1), .in_1(_8registers_encoded_1_output_11), .out(multiplexer_14_out));  // open: sel
  Multiplexer multiplexer_15 (
    .in_0(demultiplexer_13_out_1), .in_1(_8registers_encoded_1_output_12), .out(multiplexer_15_out));  // open: sel
  Multiplexer multiplexer_16 (
    .in_0(demultiplexer_14_out_1), .in_1(_8registers_encoded_1_output_13), .out(multiplexer_16_out));  // open: sel
  Multiplexer multiplexer_17 (
    .in_0(demultiplexer_15_out_1), .in_1(_8registers_encoded_1_output_14), .out(multiplexer_17_out));  // open: sel
  Multiplexer multiplexer_18 (
    .in_0(demultiplexer_16_out_1), .in_1(_8registers_encoded_1_output_15), .out(multiplexer_18_out));  // open: sel
  DataMemory Memory (
    .A_0(demultiplexer_1_out_0), .A_1(demultiplexer_2_out_0), .A_2(demultiplexer_3_out_0),
    .A_3(demultiplexer_4_out_0), .A_4(demultiplexer_5_out_0), .A_5(demultiplexer_6_out_0),
    .A_6(demultiplexer_7_out_0), .A_7(demultiplexer_8_out_0), .A_8(demultiplexer_9_out_0),
    .A_9(demultiplexer_10_out_0), .A_10(demultiplexer_11_out_0), .A_11(demultiplexer_12_out_0),
    .A_12(demultiplexer_13_out_0), .A_13(demultiplexer_14_out_0), .A_14(demultiplexer_15_out_0),
    .A_15(demultiplexer_16_out_0), .WE(instructiondecoder_1_c_0), .D_0(multiplexer_3_out),
    .D_1(multiplexer_4_out), .D_2(multiplexer_5_out), .D_3(multiplexer_6_out), .D_4(multiplexer_7_out),
    .D_5(multiplexer_8_out), .D_6(multiplexer_9_out), .D_7(multiplexer_10_out), .D_8(multiplexer_11_out),
    .D_9(multiplexer_12_out), .D_10(multiplexer_13_out), .D_11(multiplexer_14_out),
    .D_12(multiplexer_15_out), .D_13(multiplexer_16_out), .D_14(multiplexer_17_out),
    .D_15(multiplexer_18_out), .OutData_0(Memory_outdata_0), .OutData_1(Memory_outdata_1),
    .OutData_2(Memory_outdata_2), .OutData_3(Memory_outdata_3), .OutData_4(Memory_outdata_4),
    .OutData_5(Memory_outdata_5), .OutData_6(Memory_outdata_6), .OutData_7(Memory_outdata_7),
    .OutData_8(Memory_outdata_8), .OutData_9(Memory_outdata_9), .OutData_10(Memory_outdata_10),
    .OutData_11(Memory_outdata_11), .OutData_12(Memory_outdata_12), .OutData_13(Memory_outdata_13),
    .OutData_14(Memory_outdata_14), .OutData_15(Memory_outdata_15));
  _16bit_mux_2to1 WB (
    .I0_0(ALU_output_0), .I0_1(ALU_output_1), .I0_2(ALU_output_2), .I0_3(ALU_output_3), .I0_4(ALU_output_4),
    .I0_5(ALU_output_5), .I0_6(ALU_output_6), .I0_7(ALU_output_7), .I0_8(ALU_output_8), .I0_9(ALU_output_9),
    .I0_10(ALU_output_10), .I0_11(ALU_output_11), .I0_12(ALU_output_12), .I0_13(ALU_output_13),
    .I0_14(ALU_output_14), .I0_15(ALU_output_15), .I1_0(Memory_outdata_0), .I1_1(Memory_outdata_1),
    .I1_2(Memory_outdata_2), .I1_3(Memory_outdata_3), .I1_4(Memory_outdata_4), .I1_5(Memory_outdata_5),
    .I1_6(Memory_outdata_6), .I1_7(Memory_outdata_7), .I1_8(Memory_outdata_8), .I1_9(Memory_outdata_9),
    .I1_10(Memory_outdata_10), .I1_11(Memory_outdata_11), .I1_12(Memory_outdata_12),
    .I1_13(Memory_outdata_13), .I1_14(Memory_outdata_14), .I1_15(Memory_outdata_15), .Output_0(WB_output_0),
    .Output_1(WB_output_1), .Output_2(WB_output_2), .Output_3(WB_output_3), .Output_4(WB_output_4),
    .Output_5(WB_output_5), .Output_6(WB_output_6), .Output_7(WB_output_7), .Output_8(WB_output_8),
    .Output_9(WB_output_9), .Output_10(WB_output_10), .Output_11(WB_output_11), .Output_12(WB_output_12),
    .Output_13(WB_output_13), .Output_14(WB_output_14), .Output_15(WB_output_15));  // open: Select
  // Pins of 1 and 8 bits meet at Semafor_3_q_0_0
  // Pins of 1 and 8 bits meet at Semafor_2_q_0_0
  // Pins of 1 and 8 bits meet at Semafor_1_q_0_0
  // Pins of 1 and 8 bits meet at Semafor_0_q_0_0
  // Pins of 1 and 8 bits meet at add_11_s
  // Pins of 1 and 16 bits meet at add_12_s
  // Pins of 1 and 8 bits meet at add_8_s
  // Pins of 1 and 16 bits meet at add_9_s
  // Pins of 1 and 8 bits meet at add_6_s
  // Pins of 1 and 16 bits meet at add_7_s
  // Pins of 1 and 8 bits meet at add_1_s
  // Pins of 1 and 16 bits meet at add_2_s

  // Notes on the sheet:
  //   DebitTotal_0
  //   Emergency signal
  //   DebitTotal_1
  //   Rosu
  //   CS bits
  //   BA bits
  //   CF bits
  //   Galben
  //   DebitTotal_2
  //   Verde
  //   Are treaba cu Tverde
  //   4 ce au treaba cu k
  //   2 ce se ocupa de Tverde 
  //   Unde urmeaza counter
  //   Se ocupa de Tgalben init
  //   Astea 3 se ocupa de Tgalben 
  //   unde trebe counter
  //   DebitTotal_3
endmodule
